# Fritzing sketch arduino_ir_receiver (saved by Fritzing 0.8.3b)
breadboards: 1

parts:
  Part1 = Arduino Micro (Rev3)  # not connected
  IR1 = TSOP312.., 314.. [package=THT]
  C1 = Electrolytic Capacitor [capacitance=1μF package="0405 [SMD, electrolytic]"]
  LED1 = LED - 5mm [color="Red (633nm)" package="5 mm [THT]"]
  LED2 = LED - 5mm [color="Green (555nm)" package="5 mm [THT]"]
  R1 = Resistor [tolerance=±5% resistance=47 package=THT]
  IC1 = IC, DIP package, 8 pins [chip_label=IC]
  IC2 = IC, DIP package, 8 pins [chip_label=IC]
  R2 = PHOTOCELL [package=photocell]
  R3 = Resistor [tolerance=±5% resistance=10k package=THT]
  R4 = Resistor [tolerance=±5% resistance=220 package=THT]
  R5 = Resistor [tolerance=±5% resistance=220 package=THT]

nets:
  N1: IR1.GND, C1.+, R1.Pin_0
  N2: IR1.Vs, C1.-, IC1.pin4, IC2.pin4, R3.Pin_0, R4.Pin_0, R5.Pin_0
  N3: LED1.cathode, R5.Pin_1
  N4: LED2.cathode, R4.Pin_1
  N5: R1.Pin_1, R2.P$2
  N6: IC1.pin2, IC2.pin2
  N7: IC1.pin3, IC2.pin3
  N8: R2.P$1, R3.Pin_1
